# Fritzing sketch MidiMitra_Schema (saved by Fritzing 0.6.3b)
breadboards: 1

parts:
  Arduino1 = Arduino
  DIN1 = DIN-5 jack (MIDI) [package=THT]
  R1 = Resistor [tolerance=±5% resistance=220 package="0603 [SMD]"]
  R2 = Rotary Potentiometer (Large) [maximum_resistance=100kΩ package=THT]
  S1 = Pushbutton [package="[THT]"]
  R3 = Resistor [tolerance=±5% resistance=220 package="0603 [SMD]"]
  LED1 = smd LED [color="Red (633nm)" package="0603 [SMD]"]
  R4 = Resistor [tolerance=±5% resistance=220 package="0603 [SMD]"]
  Part1 = SRF05 Ultrasonic Rangefinder

nets:
  N1: Arduino1.D7, S1.Pin_3, S1.Pin_4, R3.Pin_0
  N2: Arduino1.D6, R4.Pin_0
  N3: Arduino1.D4, Part1.connector9
  N4: Arduino1.D3, Part1.connector10
  N5: Arduino1.D1TX, DIN1.5
  N6: Arduino1.+5V, R1.Pin_0, R2.leg1, S1.Pin_1, S1.Pin_2, Part1.connector8
  N7: Arduino1.GND, DIN1.2, R2.leg2, R3.Pin_1, LED1.anode, Part1.connector11
  N8: Arduino1.A0, R2.wiper
  N9: DIN1.4, R1.Pin_1
  N10: LED1.cathode, R4.Pin_1
